# Fritzing sketch fight-vest-scatch (saved by Fritzing 0.9.3b)

parts:
  Part1 = Arduino Uno (Rev3)
  Part2 = Bluetooth HC-05 Macho  # not connected
  Part3 = Arduino Pro Mini (5V)

nets:
  N1: Part1.D0/RX, Part3.RXI
  N2: Part1.D1/TX, Part3.TXO
  N3: Part1.RESET, Part3.RESET
  5V: Part1.5V, Part3.VCC
  GND: Part1.GND, Part3.GND
